# Fritzing sketch Circuit - Diagram 2 (saved by Fritzing 0.9.2b)
breadboards: 1

parts:
  Part1 = Arduino Nano (Rev3.0)
  Part2 = NCP1400 Step-Up Breakout
  VCC1 = Battery
  R1 = Resistor [tolerance=±5% resistance=220 package="1206 [SMD]"]
  U1 = SWITCH_SPDT [package=kps-1290]
  LED1 = LED - 5mm [color="Red (633nm)" package="5 mm [THT]"]
  R2 = Resistor [tolerance=±5% resistance=4.7k package=THT]
  S1 = Pushbutton [package=THT]
  C1 = Electrolytic Capacitor [capacitance=100nF package="100 mil [THT, electrolytic]"]
  R5 = Resistor [tolerance=±5% resistance=5.1k package=THT]
  RHT1 = Humidity and Temperature Sensor RHT03

nets:
  GND: Part1.GND, Part2.GND, R1.Pin_1, S1.leg0, C1.+, RHT1.GND_2
  N1: Part1.D2, R2.Pin_0, S1.leg1
  N2: Part1.D9, U1.S
  5V: Part1.5V, Part2.VOUT, VCC1.-, R2.Pin_1, C1.-, R5.Pin_0, RHT1.Vcc
  N3: Part1.A0, R5.Pin_1, RHT1.Data-signal
  N4: Part2.VIN, VCC1.+
  N5: R1.Pin_0, U1.O, LED1.cathode
  N6: U1.P, LED1.anode
