# Fritzing sketch Circuit - Datalogger v6 (saved by Fritzing 0.9.2b)
perfboards: 1

parts:
  Part1 = Arduino Pro
  BAT1 = Battery Holders [package=battery-aa-kit]
  BAT2 = Battery Holders [package=battery-aa-kit]
  BAT3 = Battery Holders [package=battery-aa-kit]
  D1 = Schottky Diode [part_number=1N5819 package="300 mil [THT]"]
  D2 = Schottky Diode [part_number=1N5819 package="300 mil [THT]"]
  BAT7 = Battery Holders [package=battery-aa-kit]
  BAT8 = Battery Holders [package=battery-aa-kit]
  BAT9 = Battery Holders [package=battery-aa-kit]
  U4 = 3.5mm Audio Jack [package=audio-jack-3.5mm-smd]
  J1 = Piezo Speaker

nets:
  N1: Part1.D7, J1.pin2
  N2: Part1.GND, BAT7.-, U4.SLEEVE
  N3: Part1.LIPO, D1.cathode
  N4: BAT1.+, D2.anode
  N5: BAT1.-, BAT2.+
  N6: BAT2.-, BAT3.+
  N7: D1.anode, BAT8.+
  N8: BAT7.+, BAT9.-
  N9: BAT8.-, BAT9.+

notes:
  Battery pack 1
  Battery pack 2
  D2 with pull-up
