# Fritzing sketch Circuit - Datalogger v8 (saved by Fritzing 0.9.3b)

parts:
  Buzzer = Piezo Speaker
  BAT1 = Battery Holders [package=battery-aa-kit]
  BAT2 = Battery Holders [package=battery-aa-kit]
  BAT3 = Battery Holders [package=battery-aa-kit]
  BAT4 = Battery Holders [package=battery-aa-kit]
  BAT5 = Battery Holders [package=battery-aa-kit]
  BAT6 = Battery Holders [package=battery-aa-kit]
  D1 = Rectifier Diode [part_number=1N5819 package="300 mil [THT]"]
  D2 = Rectifier Diode [part_number=1N5819 package="300 mil [THT]"]
  Part1 = Arduino Pro
  Rain_collector = 3.5mm Audio Jack [package=audio-jack-3.5mm-smd]
  R1 = Resistor [tolerance=±1% resistance=4.7k package=THT]

nets:
  N1: Buzzer.pin1, BAT1.-, BAT4.-, Part1.GND, Rain_collector.SLEEVE
  N2: Buzzer.pin2, Part1.D7
  N3: BAT1.+, BAT2.-
  N4: BAT2.+, BAT3.-
  N5: BAT3.+, D1.anode
  N6: BAT4.+, BAT5.-
  N7: BAT5.+, BAT6.-
  N8: BAT6.+, D2.anode
  N9: D1.cathode, D2.cathode
  N10: Part1.D2, Rain_collector.LEFT, R1.Pin_0
  N11: Part1.VCC, R1.Pin_1
