# Fritzing sketch Circuit - Datalogger v5 (saved by Fritzing 0.9.2b)
perfboards: 1

parts:
  Part1 = Arduino Pro
  BAT1 = Battery Holders [package=battery-aa-kit]
  BAT2 = Battery Holders [package=battery-aa-kit]
  BAT3 = Battery Holders [package=battery-aa-kit]
  D1 = Schottky Diode [part_number=1N5819 package="300 mil [THT]"]
  D2 = Schottky Diode [part_number=1N5819 package="300 mil [THT]"]
  BAT7 = Battery Holders [package=battery-aa-kit]
  BAT8 = Battery Holders [package=battery-aa-kit]
  BAT9 = Battery Holders [package=battery-aa-kit]
  U4 = 3.5mm Audio Jack [package=audio-jack-3.5mm-smd]
  R3 = Resistor [tolerance=±5% resistance=4.7k package=THT]
  J1 = Piezo Speaker

nets:
  N1: Part1.D7, J1.pin2
  N2: Part1.VCC, R3.Pin_0
  N3: BAT1.+, D2.anode
  N4: BAT1.-, BAT2.+
  N5: BAT2.-, BAT3.+
  N6: BAT3.-, BAT7.-, U4.SLEEVE
  N7: D1.anode, BAT8.+
  N8: BAT7.+, BAT9.-
  N9: BAT8.-, BAT9.+

notes:
  Battery pack 1
  Battery pack 2
