# Fritzing sketch Circuit - Diagram (saved by Fritzing 0.9.2b)
breadboards: 1

parts:
  Part1 = Arduino Nano (Rev3.0)
  Part2 = Tiny RTC - DS1307 Breakout Board
  Part3 = MicroSD Card Module
  LED1 = LED - 5mm [color="Red (633nm)" package="5 mm [THT]"]
  R1 = Resistor [tolerance=±5% resistance=220 package=THT]
  S1 = Pushbutton [package=THT]
  RHT1 = Humidity and Temperature Sensor RHT03
  R2 = Resistor [tolerance=±5% resistance=1M package=THT]
  R3 = Resistor [tolerance=±5% resistance=100k package=THT]

nets (from the schematic view):
  GND: Part1.GND, Part2.GND, Part3.GND, R1.Pin_1, S1.leg0, RHT1.GND_2
  N1: Part1.D2, S1.leg1
  N2: Part1.D8, LED1.anode
  N3: Part1.D10, Part3.CS
  N4: Part1.D11/MOSI, Part3.MOSI
  N5: Part1.D12/MISO, Part3.MISO
  VCC: Part1.5V, Part3.VCC, RHT1.Vcc, R2.Pin_0
  N6: Part1.A4, Part2.SCL
  N7: Part1.A2, R2.Pin_1, R3.Pin_1
  N8: Part1.A0, RHT1.Data-signal
  N9: Part1.D13/SCK, Part3.SCK
  N10: LED1.cathode, R1.Pin_0

notes:
  Rain collector
  Voltage monitoring

custom parts:
  Tiny RTC - DS1307 Breakout Board: The Tiny RTC is a breakout board for the Dallas Semiconductor/Maxim Integrated DS1307 real-time clock. The DS1307 counts seconds, minutes, hours, date of the month, month, day of the week, and year (with compensation for leap-years). The breakout board also has space for a DS18B20 digital thermometer.
